# Fritzing sketch iot (saved by Fritzing 0.9.3b)
breadboards: 1

parts:
  Capacitive_Soil_Moisture_Sensor1 = DFRobot Capacitive Soil Moisture Sensor V1.0 [part_number=SEN0193]
  YL-83_-_Detection_Board1 = YL-83 Rain Sensor - Detection Board
  DHT2 = DHT11 Humitidy and Temperature Sensor
  KY-1 = Keyes Relay [package=THT]
  LCD2 = LCD screen
  LCM1602_IIC2 = LCM1602 IIC [part_number="LCM1602 IIC" chip_label="LCM1602 IIC" package="DIP (Dual Inline) [THT]"]
  BAT1 = Battery Holders [package=lipo-1100mAh]
  S1 = Momentary Switch [package=ksa_sealed_tac_switch]
  TP1 = TP4056 [chip_label=TP4056 package="DIP (Dual Inline) [THT]"]
  R1 = Resistor [tolerance=±5% resistance=100k package=THT]
  R2 = Resistor [tolerance=±5% resistance=100k package=THT]
  M1 = DOIT Esp32 DevKit v1 (30 pins long, 11 pins width) [part_number=ESP32S-PIN30]
  부품3 = FC-28 Soil Hygrometer Module

nets:
  N1: Capacitive_Soil_Moisture_Sensor1.A, M1.D34
  VCC: Capacitive_Soil_Moisture_Sensor1.VCC, DHT2.VDD, KY-1.power, LCM1602_IIC2.VCC, S1.2, R2.Pin_0, M1.VIN, 부품3.VCC
  GND: Capacitive_Soil_Moisture_Sensor1.GND, DHT2.GND, KY-1.ground, LCM1602_IIC2.GND, TP1.pin6, R1.Pin_1, M1.GND, 부품3.GND
  N2: YL-83_-_Detection_Board1.POS, 부품3.POS
  N3: YL-83_-_Detection_Board1.NEG, 부품3.NEG
  N4: DHT2.DATA, M1.D4
  N5: KY-1.signal, M1.D14
  VSS: LCD2.VSS, LCM1602_IIC2.VSS
  VDD: LCD2.VDD, LCM1602_IIC2.VDD
  N6: LCD2.V0, LCM1602_IIC2.V0
  N7: LCD2.RS, LCM1602_IIC2.RS
  N8: LCD2.R/W, LCM1602_IIC2.RW
  N9: LCD2.E, LCM1602_IIC2.E
  N10: LCD2.DB0, LCM1602_IIC2.D0
  N11: LCD2.DB1, LCM1602_IIC2.D1
  N12: LCD2.DB2, LCM1602_IIC2.D2
  N13: LCD2.DB3, LCM1602_IIC2.D3
  N14: LCD2.DB4, LCM1602_IIC2.D4
  N15: LCD2.DB5, LCM1602_IIC2.D5
  N16: LCD2.DB6, LCM1602_IIC2.D6
  N17: LCD2.DB7, LCM1602_IIC2.D7
  N18: LCD2.LED+, LCM1602_IIC2.A
  N19: LCD2.LED-, LCM1602_IIC2.K
  N20: LCM1602_IIC2.SDA, M1.D21
  N21: LCM1602_IIC2.SCL, M1.D22
  N22: LCM1602_IIC2.LED_A, LCM1602_IIC2.LED_B
  N23: BAT1.+, BAT1.-, TP1.pin4, TP1.pin5
  N24: S1.1, TP1.pin3
  N25: R1.Pin_0, R2.Pin_1, M1.D35
  N26: M1.D13, 부품3.DO

custom parts:
  DFRobot Capacitive Soil Moisture Sensor V1.0: DFRobot Capacitive Soil Moisture Sensor V1.0 This product measures soil moisture levels by capacitive sensing, rather than resistive sensing like other types of moisture sensor. It is made of a corrosion resistant material giving it a long service life. Insert it into soil and impress your friends with the real-time soil moisture data! The product includes an on-board voltage regulator which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
  YL-83 Rain Sensor - Detection Board: The YL-83 is a rain sensor that has more resistance when dry and less resistance when wet. The module runs at 5V.
  DHT11 Humitidy and Temperature Sensor: DHT11 Humidity and Temperature Sensor
  Keyes Relay: The Keyes 5V relay module is suitable for SCM development, home appliance control. It uses a 5V~12V TIL control signal which can control DC / AC signal.
  LCM1602 IIC: I2C-Module to use a 1602 or 2004 LCD on with the wire.h libory Serial LCD Modul
  TP4056: A DIP stand-in part for whatever IC you want. With 6 pins on a 300mil dual inline package (DIP) footprint.
  DOIT Esp32 DevKit v1 (30 pins long, 11 pins width): The DOIT Esp32 DevKit v1 is one of the development board created by DOIT to evaluate the ESP-WROOM-32 module. It is based on the ESP32 microcontroller that boasts Wifi, Bluetooth, Ethernet and Low Power support all in a single chip. (vanepp) made breadboard work, adjusted pin numbering and labels and reduced size of schematic and cleaned up pcb. This chip is 30pins long (2 x15) and 11 pins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
  FC-28 Soil Hygrometer Module: The FC-28 is a soil hygrometer module that uses the Texas Instruments LM393 comparator chip to provide an analog measurement of soil humidity. The digital output is high when soil moisture is over a certain threshold, as determined by adjusting the potentiometer.
